// Logisim project Group2.circ as structural Verilog
module project_ao (
  input  [15:0] A,
  input  [15:0] B,
  input  [3:0] selector,
  output [7:0] result
);

  BitAdder bitadder_1 ();  // open: in0, out
  Adder adder_1 ();  // open: a, b, out, cin, cout
  // AND_Gate and_1 is placed but not wired
  // OR_Gate or_1 is placed but not wired
  // XOR_Gate xor_1 is placed but not wired
  Divider divider_1 ();  // open: a, b, out, upper, rem
  Multiplier multiplier_1 ();  // open: a, b, out, cin, cout
  Subtractor subtractor_1 ();  // open: a, b, out, bin, bout
  Shifter shifter_1 ();  // open: in, dist, out
  Shifter shifter_2 ();  // open: in, dist, out
  Shifter #(.shift("lr")) shifter_3 ();  // open: in, dist, out
  Shifter #(.shift("lr")) shifter_4 ();  // open: in, dist, out
  Multiplexer #(.select(4), .width(8)) multiplexer_1 (.sel(selector));  // open: in0, in1, in2, in3, in4, in5, in6, in7, in8, in9, in10, in11, in12, in13, in14, in15, out
endmodule
